// Logisim project Practica3.circ as structural Verilog: 7 circuits, main circuit Implicación
module \Implicación  (
  input  p,
  input  q,
  output p_prime_q
);

  wire not_1_p_prime;

  NOT not_1 (.in_1(p), .p_prime(not_1_p_prime));
  OR or_1 (.p(not_1_p_prime), .q(q), .p_q(p_prime_q));

  // Notes on the sheet:
  //   p_prime_q: pull=up
endmodule

module Comparador (
  input  [1:0] ab,
  input  [1:0] cd,
  output [2:0] out_3
);

  circuit_2_2 part_1 (.a(ab[1]), .b(ab[0]), .c(cd[1]), .d(cd[0]), .ab___cd(out_3[0]));
  circuit part_2 (.a(ab[1]), .b(ab[0]), .c(cd[1]), .d(cd[0]), .ab___cd(out_3[1]));
  circuit_2 part_3 (.a(ab[1]), .b(ab[0]), .c(cd[1]), .d(cd[0]), .ab___cd(out_3[2]));
endmodule

module NOT (
  input  in_1,
  output p_prime
);

  Transistor transistor_1 (.in(1'b1), .out(p_prime), .gate(in_1));
  Transistor #(.\type ("n")) transistor_2 (.in(1'b0), .out(p_prime), .gate(in_1));
endmodule

module OR (
  input  p,
  input  q,
  output p_q
);

  Transistor #(.\type ("n")) transistor_1 (.in(1'b1), .out(p_q), .gate(p));
  Transistor transistor_2 (.in(q), .out(p_q), .gate(p));
  Transistor #(.\type ("n"), .gate("br")) transistor_3 (.in(1'b1), .out(p_q), .gate(q));
endmodule

module circuit (
  input  a,
  input  b,
  input  c,
  input  d,
  output ab___cd
);

  wire and_1_out, and_2_out, and_3_out, and_4_out, not_1_out, not_2_out, not_3_out, not_4_out, not_5_out,
       not_6_out, not_7_out, not_8_out;

  not not_1 (not_1_out, a);
  not not_2 (not_2_out, b);
  not not_3 (not_3_out, c);
  not not_4 (not_4_out, d);
  not not_5 (not_5_out, b);
  not not_6 (not_6_out, d);
  not not_7 (not_7_out, a);
  not not_8 (not_8_out, c);
  and and_1 (and_1_out, not_1_out, not_2_out, not_3_out, not_4_out);
  and and_2 (and_2_out, a, not_5_out, c, not_6_out);
  and and_3 (and_3_out, not_7_out, b, not_8_out, d);
  and and_4 (and_4_out, a, b, c, d);
  or or_1 (ab___cd, and_1_out, and_2_out, and_3_out, and_4_out);
endmodule

module circuit_2 (
  input  a,
  input  b,
  input  c,
  input  d,
  output ab___cd
);

  wire and_1_out, and_2_out, and_3_out, not_1_out, not_2_out;

  not not_1 (not_1_out, c);
  not not_2 (not_2_out, d);
  and and_1 (and_1_out, a, not_1_out);
  and and_2 (and_2_out, b, not_1_out, not_2_out);
  and and_3 (and_3_out, a, b, not_2_out);
  or or_1 (ab___cd, and_1_out, and_2_out, and_3_out);
endmodule

module circuit_2_2 (
  input  a,
  input  b,
  input  c,
  input  d,
  output ab___cd
);

  wire and_1_out, and_2_out, and_3_out, not_1_out, not_2_out;

  not not_1 (not_1_out, a);
  not not_2 (not_2_out, b);
  and and_1 (and_1_out, not_1_out, c);
  and and_2 (and_2_out, not_2_out, c, d);
  and and_3 (and_3_out, not_1_out, not_2_out, d);
  or or_1 (ab___cd, and_1_out, and_2_out, and_3_out);
endmodule
